// Logisim project Instructions.circ as structural Verilog: 1 circuit, main circuit main
module main (
  input  in_1,
  input  in_2
);

  wire clock_1_out, decoder_2_out0, decoder_2_out1, or_1_out, or_2_out;
  wire [2:0] counter_4_q, or_5_out;
  wire [3:0] multiplexer_1_out_2;
  wire [11:0] bit_extender_1_out, bit_extender_2_out, counter_1_q, counter_2_q, multiplexer_1_out;
  wire [15:0] bit_extender_3_out, bit_extender_4_out, counter_3_q, ram_1_data;

  Clock clock_1 (.out(clock_1_out));
  Bit_Extender #(.in_width(16), .out_width(12)) bit_extender_1 (
    .in({multiplexer_1_out_2, multiplexer_1_out}), .out(bit_extender_1_out));
  Counter #(.width(12), .max('hfff)) counter_1 (
    .load(or_2_out), .D(bit_extender_1_out), .count(in_1), .Q(counter_1_q), .clk(clock_1_out), .clr(in_1));  // open: carry
  Bit_Extender #(.in_width(16), .out_width(12)) bit_extender_2 (
    .in({multiplexer_1_out_2, multiplexer_1_out}), .out(bit_extender_2_out));
  Counter #(.width(12), .max('hfff)) counter_2 (
    .D(bit_extender_2_out), .count(or_1_out), .Q(counter_2_q), .clk(clock_1_out));  // open: load, carry, clr
  Counter #(.width(16), .max('hffff)) counter_3 (
    .load(or_1_out), .D({multiplexer_1_out_2, multiplexer_1_out}), .count(in_1), .Q(counter_3_q),
    .clk(clock_1_out));  // open: carry, clr
  assign bit_extender_3_out = {{4{1'b0}}, counter_1_q};  // Bit_Extender bit_extender_3
  assign bit_extender_4_out = {{4{1'b0}}, counter_2_q};  // Bit_Extender bit_extender_4
  buf or_1 (or_1_out, decoder_2_out1);  // OR_Gate
  RAM #(.addrWidth(12), .dataWidth(16)) ram_1 (
    .addr(counter_1_q), .data(ram_1_data), .clk(clock_1_out));  // open: sel, ld, clr
  buf or_2 (or_2_out, decoder_2_out0);  // OR_Gate
  Counter #(.width(3), .max('h7)) counter_4 (.Q(counter_4_q), .clk(clock_1_out));  // open: load, D, count, carry, clr
  Multiplexer #(.select(3), .width(16), .enable("false")) multiplexer_1 (
    .in1(bit_extender_3_out), .in2(bit_extender_4_out), .in5(counter_3_q), .in7(ram_1_data),
    .out({multiplexer_1_out_2, multiplexer_1_out}), .sel(or_5_out));  // open: in0, in3, in4, in6
  Decoder #(.select(3), .enable("false")) decoder_1 ();  // open: out0, out1, out2, out3, out4, out5, out6, out7, sel
  Decoder #(.select(3), .enable("false")) decoder_2 (
    .out0(decoder_2_out0), .out1(decoder_2_out1), .sel(counter_4_q));  // open: out2, out3, out4, out5, out6, out7
  buf or_3 (or_5_out[2], decoder_2_out1);  // OR_Gate
  or or_4 (or_5_out[1], decoder_2_out1, decoder_2_out0);
  buf or_5 (or_5_out[0], decoder_2_out1);  // OR_Gate

  // Notes on the sheet:
  //   AR
  //   PC
  //   IR
endmodule
